# Fritzing sketch dbl tactile switch v0.3 (saved by Fritzing 0.9.3b)
circuit board: 2.50978cm x 1.73884cm
breadboards: 1

parts:
  J1 = Dagu DGServo 9g header (male) [package=THT]
  S1 = SWITCH-MOMENTARY-2 [package=tactile-pth]
  S2 = SWITCH-MOMENTARY-2 [package=tactile-pth]

nets:
  N1: J1.gnd, S2.2
  N2: J1.Vcc, S1.2, S2.1
  N3: J1.pulse, S1.1

notes:
  DBL SW v0.3
